# Fritzing sketch porgjs-control-plate (saved by Fritzing 0.9.3b)
stripboards: 2

parts:
  U1 = Optocoupler [package=THT]
  LED1 = smd LED [color="Green (555nm)" package="1206 [SMD]"]
  R1 = Resistor [tolerance=±5% resistance=220 package="0805 [SMD]"]
  Part1 = Arduino Nano (Rev3.0)

nets:
  N1: U1.Pin_1, R1.Pin_1
  N2: U1.Pin_2, LED1.cathode, Part1.GND
  N3: LED1.anode, R1.Pin_0, Part1.D4
